# Fritzing sketch Arduino_Esp8266Sketch (saved by Fritzing 0.9.3b)
breadboards: 1

parts:
  Part2 = Arduino Uno (Rev3)
  U2 = ESP8266 WiFi Module [part_number=ESP8266]
  DHT1 = DHT11 Humitidy and Temperature Sensor
  R1 = Photocell (LDR) [package=THT]
  R2 = Resistor [tolerance=±5% resistance=220 package="0603 [SMD]"]

nets:
  N1: Part2.A0, R1.pin_1, R2.Pin_0
  N2: Part2.D0/RX, U2.RXD
  N3: Part2.D1/TX, U2.TXD
  GND: Part2.RESET, Part2.GND, U2.GND, DHT1.GND, R2.Pin_1
  3V3: Part2.3V3, U2.VCC, U2.CH_PD, DHT1.VDD
  N4: Part2.5V, R1.pin_0
  N5: U2.GPIO_2, DHT1.DATA

custom parts:
  ESP8266 WiFi Module: Generic WiFi Module based on the ESP8266 with onboard PCB antenna and UART communications
  DHT11 Humitidy and Temperature Sensor: DHT11 Humidity and Temperature Sensor
